# Fritzing sketch DumpIR (saved by Fritzing 0.9.2b)
circuit board: 5.05504cm x 5.31138cm
breadboards: 1

parts:
  UNO = Arduino Uno (Rev3)
  Vishay_TSOP58438 = TSOP582.., 584.. [package=THT]

nets:
  N1: UNO.D11_PWM/MOSI, Vishay_TSOP58438.Data
  GND: UNO.GND, Vishay_TSOP58438.GND
  5V: UNO.5V, Vishay_TSOP58438.Vs

custom parts:
  TSOP582.., 584..: The TSOP582.., TSOP584.. series are miniaturized receivers for infrared remote control systems. A PIN diode and a preamplifier are assembled on a lead frame, the epoxy package acts as an IR filter. The demodulated output signal can be directly decoded by a microprocessor. The TSOP582.. is compatible with all common IR remote control data formats. The TSOP584.. is optimized to suppress almost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
