# Fritzing sketch Programming board (saved by Fritzing 0.9.2b)
circuit board: 5.5cm x 5.5cm
breadboards: 1

parts:
  ESP12 = HUZZAH ESP8266 Breakout
  V1 = DC Power [voltage=9V]
  UNO = Arduino Uno (Rev3)

nets:
  N1: ESP12.TXD, UNO.D1/TX
  N2: ESP12.RXD_5V, UNO.D0/RX
  GND: ESP12.GND, V1.V-, UNO.GND
  N3: ESP12.VBAT, V1.V+, UNO.VIN
  N4: ESP12.GPIO0, UNO.D11_PWM/MOSI

notes:
  ESP8266
  antenna

custom parts:
  HUZZAH ESP8266 Breakout: The ESP8266 processor from Espressif is an 80 MHz microcontroller with a full WiFi front-end (both as client and access point) and TCP/IP stack with DNS support as well.
